# Fritzing sketch iss_notification (saved by Fritzing 0.8.0b)
breadboards: 1

parts:
  LED1 = LED - 5mm [color="Infrared (940nm)" part_number=TSAL6400 current=100mA package="5 mm [THT]"]
  R1 = Resistor [tolerance=±5% resistance=47 package=THT]
  Arduino_UNO_R3 = Arduino Uno (Rev3)

nets:
  N1: LED1.cathode, Arduino_UNO_R3.GND
  N2: LED1.anode, R1.Pin_0
  N3: R1.Pin_1, Arduino_UNO_R3.D3_PWM

notes:
  TSAL6400 - 940nm IR LED
  GND
  Pin 3 - PWM
